# Fritzing sketch multiplex_potentiometers (saved by Fritzing 0.9.2b)
circuit board: 7.65563cm x 3.84116cm
breadboards: 1

parts:
  R1 = Rotary Potentiometer (Small) [maximum_resistance=100kΩ package=THT]
  R2 = Rotary Potentiometer (Small) [maximum_resistance=100kΩ package=THT]
  R3 = Rotary Potentiometer (Small) [maximum_resistance=100kΩ package=THT]
  R4 = Rotary Potentiometer (Small) [maximum_resistance=100kΩ package=THT]
  R5 = Rotary Potentiometer (Small) [maximum_resistance=100kΩ package=THT]
  R8 = Rotary Potentiometer (Small) [maximum_resistance=100kΩ package=THT]
  R6 = Rotary Potentiometer (Small) [maximum_resistance=100kΩ package=THT]
  R7 = Rotary Potentiometer (Small) [maximum_resistance=100kΩ package=THT]
  Part1 = Arduino Uno (Rev3)

nets:
  N1: R1.leg1, R2.leg1, R3.leg1, R4.leg1, Part1.D5_PWM
  N2: R1.wiper, R5.wiper, Part1.A0
  N3: R1.leg2, R2.leg2, R3.leg2, R4.leg2, Part1.D3_PWM
  N4: R2.wiper, R6.wiper, Part1.A1
  N5: R3.wiper, R7.wiper, Part1.A2
  N6: R4.wiper, R8.wiper, Part1.A3
  N7: R5.leg1, R8.leg1, R6.leg1, R7.leg1, Part1.D4
  N8: R5.leg2, R8.leg2, R6.leg2, R7.leg2, Part1.D2
