# Fritzing sketch keyboard (saved by Fritzing 0.9.2b)
breadboards: 1

parts:
  IC1 = 74LS164N [chip_label=74LS164N package="DIP (Dual Inline) [THT]"]
  IC2 = 74xx251 [chip_label=74xx251 package="DIP (Dual Inline) [THT]"]
  J1 = female pin header, 16 pins [form="♀ (female)"]
  Part1 = Arduino Uno (Rev3)

nets:
  N1: IC1.DSA, IC1.DSB, IC2.Y, Part1.D4
  N2: IC1.Q0, J1.pin16
  N3: IC1.Q1, J1.pin11
  N4: IC1.Q2, J1.pin10
  N5: IC1.Q3, J1.pin9
  GND: IC1.GND, IC2.GND
  N6: IC1.CP, Part1.D8
  5V: IC1./MR, IC1.Vcc, IC2.Vcc
  N7: IC1.Q4, J1.pin8
  N8: IC1.Q5, J1.pin7
  N9: IC1.Q6, J1.pin6
  N10: IC1.Q7, J1.pin1
  N11: IC2.D3, J1.pin5
  N12: IC2.D2, J1.pin4
  N13: IC2.D1, J1.pin3
  N14: IC2.D0, J1.pin2
  N15: IC2.G, Part1.D3_PWM
  N16: IC2.C, Part1.D5_PWM
  N17: IC2.B, Part1.D6_PWM
  N18: IC2.A, Part1.D7
  N19: IC2.D7, J1.pin15
  N20: IC2.D6, J1.pin14
  N21: IC2.D5, J1.pin13
  N22: IC2.D4, J1.pin12

custom parts:
  74LS164N: 8-bit serial-in, parallel-out shift register
  74xx251: A DIP stand-in part for whatever IC you want. With 16 pins on a 300mil dual inline package (DIP) footprint.
