# Fritzing sketch clock (saved by Fritzing 0.9.9b)
circuit board: 7.65079cm x 11.1743cm
breadboards: 1

parts:
  ZS-042_RTC1 = ZS-042 RTC Module
  U1 = ATTINY45 [package=dip]
  S1 = Pushbutton [package="[THT]"]
  S2 = Pushbutton [package="[THT]"]
  S3 = Pushbutton [package="[THT]"]
  R1 = Resistor [tolerance=±5% resistance=10k package="0805 [SMD]"]
  R2 = Resistor [tolerance=±5% resistance=10k package="0805 [SMD]"]
  R3 = Resistor [tolerance=±5% resistance=22k package="0805 [SMD]"]
  M1 = MAX7219 8x8 single Led Matrix Module
  M2 = MAX7219 8x8 single Led Matrix Module
  M3 = MAX7219 8x8 single Led Matrix Module

nets:
  GND: ZS-042_RTC1.GND, U1.GND, R3.Pin_0, M1.I-GND-1, M1.O-GND-1, M1.I-GND-2, M1.O-GND-2, M1.I-GND-3, M1.O-GND-3, M1.I-GND-4, M1.O-GND-4, M2.I-GND-1, M2.O-GND-1, M2.I-GND-2, M2.O-GND-2, M2.I-GND-3, M2.O-GND-3, M2.I-GND-4, M2.O-GND-4, M3.I-GND-1, M3.O-GND-1, M3.I-GND-2, M3.O-GND-2, M3.I-GND-3, M3.O-GND-3, M3.I-GND-4, M3.O-GND-4
  5V: ZS-042_RTC1.VCC, U1.VCC, S3.Pin_1, S3.Pin_2, R2.Pin_1, M1.I-VCC-1, M1.O-VCC-1, M1.I-VCC-2, M1.O-VCC-2, M1.I-VCC-3, M1.O-VCC-3, M1.I-VCC-4, M1.O-VCC-4, M2.I-VCC-1, M2.O-VCC-1, M2.I-VCC-2, M2.O-VCC-2, M2.I-VCC-3, M2.O-VCC-3, M2.I-VCC-4, M2.O-VCC-4, M3.I-VCC-1, M3.O-VCC-1, M3.I-VCC-2, M3.O-VCC-2, M3.I-VCC-3, M3.O-VCC-3, M3.I-VCC-4, M3.O-VCC-4
  N1: ZS-042_RTC1.SDA, U1.PB0(MOSI), M1.I-DIN-1
  N2: ZS-042_RTC1.SCL, U1.PB2(SCK_ADC1)
  N3: ZS-042_RTC1.SQW, U1.PB1(MISO)
  N4: U1.PB5(NRES), M1.I-CS-1, M1.O-CS-1, M1.I-CS-2, M1.O-CS-2, M1.I-CS-3, M1.O-CS-3, M1.I-CS-4, M1.O-CS-4, M2.I-CS-1, M2.O-CS-1, M2.I-CS-2, M2.O-CS-2, M2.I-CS-3, M2.O-CS-3, M2.I-CS-4, M2.O-CS-4, M3.I-CS-1, M3.O-CS-1, M3.I-CS-2, M3.O-CS-2, M3.I-CS-3, M3.O-CS-3, M3.I-CS-4, M3.O-CS-4
  N5: U1.PB3(ADC3), S1.Pin_3, S1.Pin_4, S2.Pin_3, S2.Pin_4, S3.Pin_3, S3.Pin_4, R3.Pin_1
  N6: U1.PB4(ADC2), M1.I-CLK-1, M1.O-CLK-1, M1.I-CLK-2, M1.O-CLK-2, M1.I-CLK-3, M1.O-CLK-3, M1.I-CLK-4, M1.O-CLK-4, M2.I-CLK-1, M2.O-CLK-1, M2.I-CLK-2, M2.O-CLK-2, M2.I-CLK-3, M2.O-CLK-3, M2.I-CLK-4, M2.O-CLK-4, M3.I-CLK-1, M3.O-CLK-1, M3.I-CLK-2, M3.O-CLK-2, M3.I-CLK-3, M3.O-CLK-3, M3.I-CLK-4, M3.O-CLK-4
  N7: S1.Pin_1, S1.Pin_2, R1.Pin_0
  N8: S2.Pin_1, S2.Pin_2, R1.Pin_1, R2.Pin_0
  N9: M1.O-DOUT-1, M1.I-DIN-2
  N10: M1.O-DOUT-2, M1.I-DIN-3
  N11: M1.O-DOUT-3, M1.I-DIN-4
  N12: M1.O-DOUT-4, M2.I-DIN-1
  N13: M2.O-DOUT-1, M2.I-DIN-2
  N14: M2.O-DOUT-2, M2.I-DIN-3
  N15: M2.O-DOUT-3, M2.I-DIN-4
  N16: M2.O-DOUT-4, M3.I-DIN-1
  N17: M3.O-DOUT-1, M3.I-DIN-2
  N18: M3.O-DOUT-2, M3.I-DIN-3
  N19: M3.O-DOUT-3, M3.I-DIN-4

custom parts:
  MAX7219 8x8 single Led Matrix Module: Description: MAX7219 8x8 LedMatrix single Red Module Dimensions: 32x32mm Documents:
