# Fritzing sketch schema (saved by Fritzing 0.9.9b)
circuit board: 5.39006cm x 1.6618cm
circuit board: 5.40955cm x 2.31558cm
breadboards: 2

parts:
  LED1 = smd LED [color="Infrared (940nm)" package="1206 [SMD]"]
  LED2 = smd LED [color="Infrared (940nm)" package="1206 [SMD]"]
  R1 = Resistor [tolerance=±5% power=0.25 resistance=100k package=THT]
  R2 = Resistor [tolerance=±5% power=0.25 resistance=100k package=THT]
  VCC1 = Battery
  R3 = Resistor [tolerance=±5% power=0.25 resistance=47 package=THT]
  Composant1 = Arduino Uno (Rev3)
  J1 = Basic Servo
  IR_sensor_2 = LED - 3mm [color="White (8000K)" current=0.030 package="3 mm [THT]"]
  IR_sensor_1 = LED - 3mm [color="White (8000K)" package="3 mm [THT]"]

nets:
  N1: LED1.cathode, LED2.cathode, R3.Pin_0
  N2: LED1.anode, LED2.anode, VCC1.+
  5V: R1.Pin_0, R2.Pin_0, Composant1.5V, J1.vcc
  N3: R1.Pin_1, Composant1.A5/SCL, IR_sensor_2.cathode
  N4: R2.Pin_1, Composant1.A4/SDA, IR_sensor_1.cathode
  N5: VCC1.-, R3.Pin_1
  N6: Composant1.D11_PWM/MOSI, J1.pulse
  GND: Composant1.GND, J1.gnd, IR_sensor_2.anode, IR_sensor_1.anode
