# Fritzing sketch schema (saved by Fritzing 0.9.9b)
circuit board: 7.49132cm x 5.86952cm
stripboards: 1

parts:
  R1 = Resistor [tolerance=±5% power=0.25 resistance=1k package=THT]
  S2 = Pushbutton [package="[THT]"]
  Arduino_Nano = Arduino Nano (Rev3.0)
  Q1 = NPN-Transistor [part_number="BC 549 B" package="TO92 [THT]"]
  SPKR1 = Loudspeaker
  S1 = Pushbutton [package="[THT]"]
  R3 = Resistor [tolerance=±5% power=0.25 resistance=22k package=THT]
  R4 = Resistor [tolerance=±5% power=0.25 resistance=22k package=THT]
  7_Segment1 = 7 Segment Display
  7_Segment2 = 7 Segment Display
  7_Segment3 = 7 Segment Display
  J1 = female pin header, 11 pins [form="♀ (female)"]

nets:
  N1: R1.Pin_0, Arduino_Nano.A3
  N2: R1.Pin_1, Q1.B
  5V: S2.Pin_1, S2.Pin_2, Arduino_Nano.5V, SPKR1.pin1, S1.Pin_1, S1.Pin_2
  N3: S2.Pin_3, S2.Pin_4, Arduino_Nano.A5, R4.Pin_1
  GND: Arduino_Nano.GND, Q1.E, R3.Pin_0, R4.Pin_0
  D2: Arduino_Nano.D2, 7_Segment1.Segment_DP, 7_Segment2.Segment_DP, 7_Segment3.Segment_DP, J1.pin1
  D3: Arduino_Nano.D3, 7_Segment3.common_anode, J1.pin2
  D4: Arduino_Nano.D4, 7_Segment2.common_anode, J1.pin3
  D5: Arduino_Nano.D5, 7_Segment1.common_anode, J1.pin4
  D6: Arduino_Nano.D6, 7_Segment1.Segment_A, 7_Segment2.Segment_A, 7_Segment3.Segment_A, J1.pin5
  D7: Arduino_Nano.D7, 7_Segment1.Segment_B, 7_Segment2.Segment_B, 7_Segment3.Segment_B, J1.pin6
  D8: Arduino_Nano.D8, 7_Segment1.Segment_F, 7_Segment2.Segment_F, 7_Segment3.Segment_F, J1.pin7
  D9: Arduino_Nano.D9, 7_Segment1.Segment_G, 7_Segment2.Segment_G, 7_Segment3.Segment_G, J1.pin8
  D10: Arduino_Nano.D10, 7_Segment1.Segment_C, 7_Segment2.Segment_C, 7_Segment3.Segment_C, J1.pin9
  D11: Arduino_Nano.D11/MOSI, 7_Segment1.Segment_D, 7_Segment2.Segment_D, 7_Segment3.Segment_D, J1.pin10
  D12: Arduino_Nano.D12/MISO, 7_Segment1.Segment_E, 7_Segment2.Segment_E, 7_Segment3.Segment_E, J1.pin11
  N4: Arduino_Nano.A4, S1.Pin_3, S1.Pin_4, R3.Pin_1
  N5: Q1.C, SPKR1.pin2
