# Fritzing sketch testPower (saved by Fritzing 0.9.9b)
breadboards: 1

parts:
  Composant1 = Arduino Uno (Rev3)
  S1 = Pushbutton [package="[THT]"]
  C1 = Electrolytic Capacitor [capacitance=1µF voltage=35V package="100 mil [THT, electrolytic]"]
  R1 = Resistor [tolerance=±5% power=0.25 resistance=1k package=THT]
  R2 = Resistor [tolerance=±5% power=0.25 resistance=220 package=THT]
  Q1 = NPN-Transistor [package="TO92 [THT]"]

nets:
  GND: Composant1.GND, C1.-
  N1: Composant1.D3_PWM, C1.+, R1.Pin_1, R2.Pin_0
  N2: Composant1.5V, Q1.E
  N3: S1.Pin_1, S1.Pin_2, R2.Pin_1
  5V: S1.Pin_3, S1.Pin_4, Q1.C
  N4: R1.Pin_0, Q1.B
