# Fritzing sketch schema (saved by Fritzing 0.9.9b)
breadboards: 1

parts:
  R1 = Resistor [tolerance=±5% power=0.25 resistance=1k package=THT]
  S2 = Pushbutton [package="[THT]"]
  Arduino_Micro = Arduino Nano (Rev3.0)
  Q1 = NPN-Transistor [part_number="BC 549 B" package="TO92 [THT]"]
  SPKR1 = Loudspeaker
  S1 = Pushbutton [package="[THT]"]

nets:
  N1: R1.Pin_0, Arduino_Micro.A3
  N2: R1.Pin_1, Q1.B
  GND: S2.Pin_1, S2.Pin_2, Arduino_Micro.GND, Q1.E, S1.Pin_1, S1.Pin_2
  N3: S2.Pin_3, S2.Pin_4, Arduino_Micro.A1
  N4: Arduino_Micro.A0, S1.Pin_3, S1.Pin_4
  N5: Arduino_Micro.3V3, SPKR1.pin1
  N6: Q1.C, SPKR1.pin2
