# Fritzing sketch led6 (saved by Fritzing 0.9.2b)
circuit board: 5.53292cm x 6.82532cm
breadboards: 1

parts:
  R1 = Resistor [tolerance=±5% resistance=6.8k package=THT]
  R3 = Resistor [tolerance=±5% resistance=6.8k package=THT]
  R5 = Resistor [tolerance=±5% resistance=6.8k package=THT]
  LED2' = LED - 5mm [color="Red (633nm)" package="5 mm [THT]"]
  LED2 = LED - 5mm [color="Red (633nm)" package="5 mm [THT]"]
  LED1' = LED - 5mm [color="Red (633nm)" package="5 mm [THT]"]
  LED3 = LED - 5mm [color="Red (633nm)" package="5 mm [THT]"]
  LED1 = LED - 5mm [color="Red (633nm)" package="5 mm [THT]"]
  R7 = Resistor [tolerance=±5% resistance=100 package=THT]
  R8 = Resistor [tolerance=±5% resistance=100 package=THT]
  R9 = Resistor [tolerance=±5% resistance=100 package=THT]
  LED3' = LED - 5mm [color="Red (633nm)" package="5 mm [THT]"]
  Q2 = NPN-Transistor [package="TO92 [THT]"]
  Q4 = NPN-Transistor [package="TO92 [THT]"]
  Q6 = NPN-Transistor [package="TO92 [THT]"]
  Q1 = PNP-Transistor [package="TO92 [THT]"]
  Q3 = PNP-Transistor [package="TO92 [THT]"]
  Q5 = PNP-Transistor [package="SOT-23 [SMD]"]
  LED1a = LED - 5mm [color="Red (633nm)" package="5 mm [THT]"]
  LED3a = LED - 5mm [color="Red (633nm)" package="5 mm [THT]"]
  LED2a = LED - 5mm [color="Red (633nm)" package="5 mm [THT]"]
  LED1b = LED - 5mm [color="Red (633nm)" package="5 mm [THT]"]
  LED2b = LED - 5mm [color="Red (633nm)" package="5 mm [THT]"]
  LED3b = LED - 5mm [color="Red (633nm)" package="5 mm [THT]"]
  R10 = Resistor [tolerance=±5% resistance=100 package=THT]
  R11 = Resistor [tolerance=±5% resistance=100 package=THT]
  R12 = Resistor [tolerance=±5% resistance=100 package=THT]

nets:
  N1: R1.Pin_0, Q2.B, Q1.B
  N2: R3.Pin_0, Q4.B, Q3.B
  N3: R5.Pin_0, Q6.B, Q5.0
  N4: LED2'.cathode, LED2.anode, R8.Pin_1, Q4.C, Q3.E
  N5: LED2'.anode, LED2.cathode, R9.Pin_0
  N6: LED1'.cathode, LED1.anode, R7.Pin_1, Q2.C, Q1.E
  N7: LED1'.anode, LED1.cathode, R8.Pin_0
  N8: LED3.cathode, R7.Pin_0, LED3'.anode
  N9: LED3.anode, R9.Pin_1, LED3'.cathode, Q6.C, Q5.2
  5V: Q2.E, Q4.E, Q6.E
  GND: Q1.C, Q3.C, Q5.1
  N10: LED1a.cathode, LED1b.anode, R10.Pin_0
  N11: LED1a.anode, LED1b.cathode, R12.Pin_1
  N12: LED3a.cathode, LED3b.anode, R12.Pin_0
  N13: LED3a.anode, LED3b.cathode, R11.Pin_1
  N14: LED2a.cathode, LED2b.anode, R11.Pin_0
  N15: LED2a.anode, LED2b.cathode, R10.Pin_1

notes:
  A
  B
  C

custom parts:
  NPN-Transistor: A standard NPN-transistor
