# Fritzing sketch printer (saved by Fritzing 0.9.9b)
breadboards: 2

parts:
  PaperSensor = CNZ1120 [package=cnz1120]
  HeadDecoder = ILD213T [package=so08]
  PaperDecoder = ILD213T [package=so08]
  J1f = female pin header, 7 pins [form="♀ (female)"]
  J1m = male pin header, 7 pins [form="♂ (male)"]
  R1 = Resistor [tolerance=±5% power=0.25 resistance=100 package=THT]
  Composant1 = Arduino Uno (Rev3)
  HeadSensor = Pushbutton [package=THT]
  J2f = female pin header, 10 pins [form="♀ (female)"]
  J2m = male pin header, 10 pins [form="♂ (male)"]
  R2 = Resistor [tolerance=±5% power=0.25 resistance=100 package=THT]
  M1 = DC Motor
  M2 = DC Motor
  IC1 = H-Bridge [package=THT]

nets:
  N1: PaperSensor.1, J1f.pin1
  N2: PaperSensor.2, PaperSensor.4, J1f.pin2
  N3: PaperSensor.3, J1f.pin3
  N4: HeadDecoder.A1, HeadDecoder.A2, J2f.pin8, J2m.pin8, R2.Pin_0
  GND: HeadDecoder.C1, HeadDecoder.C2, J1m.pin2, J1m.pin5, HeadSensor.leg0, J2f.pin2, J2m.pin2, IC1.GND3, IC1.GND4
  N5: HeadDecoder.ET1, Composant1.A1, J2f.pin9, J2m.pin9
  5V: HeadDecoder.CT1, HeadDecoder.CT2, J1m.pin6, R1.Pin_0, J2f.pin1, J2m.pin1, R2.Pin_1, IC1.VCC1
  N6: HeadDecoder.ET2, Composant1.A0, J2f.pin10, J2m.pin10
  N7: PaperDecoder.A1, PaperDecoder.A2, PaperDecoder.CT1, PaperDecoder.CT2, J1f.pin6
  N8: PaperDecoder.C1, PaperDecoder.C2, J1f.pin5
  N9: PaperDecoder.ET1, J1f.pin7
  N10: PaperDecoder.ET2, J1f.pin4
  N11: J1m.pin1, R1.Pin_1
  N12: J1m.pin3, Composant1.A4/SDA
  N13: J1m.pin4, Composant1.A3
  N14: J1m.pin7, Composant1.A2
  N15: Composant1.D9_PWM, IC1.3A
  N16: Composant1.D10_PWM/SS, IC1.4A
  N17: Composant1.D11_PWM/MOSI, IC1.3_4EN
  N18: Composant1.A5/SCL, HeadSensor.leg1
  N19: Composant1.D3_PWM, IC1.1_2EN
  N20: Composant1.D5_PWM, IC1.1A
  N21: Composant1.D6_PWM, IC1.2A
  N22: J2f.pin3, J2m.pin3
  N23: J2f.pin4, J2m.pin4
  N24: J2f.pin5, J2m.pin5
  N25: J2f.pin6, J2m.pin6
  N26: J2f.pin7, J2m.pin7
  N27: M1.pin_1, IC1.1Y
  N28: M1.pin_2, IC1.2Y
  N29: M2.pin_1, IC1.3Y
  N30: M2.pin_2, IC1.4Y
  GND1: IC1.GND1, IC1.GND2
  12V: IC1.VCC2
